# Fritzing sketch esquema_receptor (saved by Fritzing 0.9.2b)

parts:
  Parte1 = Arduino Uno (Rev3)  # not connected
  Parte2 = LED Matrix - Serial Interface - Red/Green/Blue  # not connected
  Parte3 = DeuLigne 1.1 - The Snootlab's LCD shield for Arduino  # not connected
  Parte4 = Arduino Xbee Libellium Shield
  U1 = XBEE-1 [package=xbee-1]

nets:
  N1: Parte4.I/08, U1.DIO0
  N2: Parte4.I/02, U1.DIO1
  N3: Parte4.I/03, U1.DIO2
  N4: Parte4.I/06, U1.DIO3
  N5: Parte4.I/05, U1.RTS
  N6: Parte4.15, U1.DIO5
  N7: Parte4.14, Parte4.8, U1.RES
  N8: Parte4.13, U1.DIO9
  N9: Parte4.I/07, U1.CTS
  N10: Parte4.I/04, U1.DIO4
  GND: Parte4.GND, U1.GND
  N11: Parte4.9, U1.DTR
  N12: Parte4.PWM1, U1.DIO11
  N13: Parte4.PWM0, U1.RSSI
  N14: Parte4.RST, U1.RESET
  N15: Parte4.4, U1.DIO12
  N16: Parte4.DIN, U1.DIN
  N17: Parte4.DOUT, U1.DOUT
  +3V3: Parte4.+3V3, U1.VDD
